# Fritzing sketch handheldspedo (saved by Fritzing 0.9.3b)
circuit board: 6.29169cm x 5.9667cm
breadboards: 1

parts:
  part = Raspberry Pi 3 [part_number=RPI-3-V1.2]
  part_2 = Triple Axis Accelerometer Breakout - ADXL345

nets:
  3V3: part.3v3, part_2.VCC
  N1: part.GPIO2, part_2.SDA
  N2: part.GPIO3, part_2.SCL
  GND: part.GND, part_2.GND

notes:
  Dariusz Kulpinski
  CENG 317
  Breadboard Wiring Diagram
  RED [VCC - 3.3V (Pin 1)]
  BLACK [GND - GND (Pin 38)]
  BLUE [SDA - SDA1 I2C (Pin 2)]
  YELLOW [SCL - SCL1 I2C (Pin 3)]
  Dariusz Kulpinski
  CENG317 Project
  Handheld Spedometer
  PCB Top
  PCB Bottom
  <- Raspberry Pi 3 V+ GPIO
  ADXL345 Accelerometer
  GND
  VCC (3.3V)
  SCL
  SDA
